# Fritzing sketch Akilli_guvenlik_sistemi (saved by Fritzing 0.9.4)
breadboards: 2

parts:
  U1 = LuaNode32 / ESP32 [part_number=ESP32S-PIN30]
  Parça1 = RFID-RC522-v2
  PIR1 = PIR sensor
  LED1 = LED - 5mm [color="Orange (620nm)" package="5 mm [THT]"]
  J1 = Piezo Speaker
  LED2 = LED - 5mm [color="Red (633nm)" package="5 mm [THT]"]
  LED3 = LED - 5mm [color="Green (555nm)" package="5 mm [THT]"]
  R1 = Resistor [tolerance=±5% resistance=330 package=THT]
  R2 = Resistor [tolerance=±5% resistance=330 package=THT]
  LED4 = LED - 5mm [color="Red (633nm)" package="5 mm [THT]"]
  R3 = Resistor [tolerance=±5% resistance=330 package=THT]
  S1 = SWITCH-MOMENTARY-2 [package=tactile_switch_tall]
  R4 = Resistor [tolerance=±5% resistance=10k package=THT]

nets:
  N1: U1.D25, R4.Pin_1
  N2: U1.D26, R3.Pin_1
  N3: U1.D27, PIR1.SIG, LED1.anode
  GND: U1.GND, Parça1.GND, PIR1.GND, LED1.cathode, J1.pin2, LED2.cathode, LED3.cathode, LED4.cathode, R4.Pin_0
  3V3: U1.3V3, Parça1.3.3V
  N4: U1.D2, J1.pin1
  N5: U1.D4, Parça1.RST
  N6: U1.D5, Parça1.SDA
  N7: U1.D18, Parça1.SCK
  N8: U1.D19, Parça1.MISO
  N9: U1.D21, R2.Pin_1
  N10: U1.D22, R1.Pin_1
  N11: U1.D23, Parça1.MOSI
  N12: PIR1.VDD, S1.2
  N13: LED2.anode, R2.Pin_0
  N14: LED3.anode, R1.Pin_0
  N15: LED4.anode, R3.Pin_0

notes:
  EMRE ERKANİ
  201813152035
  AKILLI GÜVENLİK SİSTEMİ

custom parts:
  LuaNode32 / ESP32: New Image for LuaNode32 DOIT ESP32 DEVKIT V1. Base parts from LuaNode32 / ESP32 ESP32 based LuaNode32 by G.Noorlander DOIT Esp32 DevKit v1 (30 pins long, 11 pins width) by Werner Rothschopf (modified by vanepp Dec 2018)
  RFID-RC522-v2: A simple China made RFID-RC522 Reader; do check the pin labels, as this is a MFRC522 based clone.
